// Digital circuit CPU.dig as structural Verilog
module CPU (
  input  CLOCK,
  output [15:0] out_2
);

  wire [7:0] add_1_s, PC_q;

  Register #(.Bits(8), .isProgramCounter("true")) PC (.D(add_1_s), .C(CLOCK), .en(CLOCK), .Q(PC_q));
  Add #(.Bits(8)) add_1 (.a(8'h4), .b(PC_q), .c_i(1'b0), .s(add_1_s));  // open: c_o
  ROM #(.AddrBits(8), .Bits(16), .isProgramMemory("true")) Instruction_Memory (.A(PC_q), .sel(1'b1), .D(out_2));

  // Notes on the sheet:
  //   contents of Instruction_Memory (hex, n*v repeats v):
  //   0,21
endmodule
